// Logisim project alu.circ as structural Verilog: 12 circuits, main circuit main
module main (
  input  [3:0] in_1,
  input  [3:0] in_2
);

  _4_bit_full_adder u_4_bit_full_adder_1 ();  // open: A_In, B_In, Output, Carry_Out, Carry_In
  _4_bit_subtractor u_4_bit_subtractor_1 ();  // open: B_In, A_In, Output, Overflow___Underflow
  _4_bit_increment u_4_bit_increment_1 ();  // open: Input, Carry_Out, Output
  _4_bit_decrementer u_4_bit_decrementer_1 ();  // open: A_In, Output, Carry_Out
  _4_bit_right_left_shift u_4_bit_right_left_shift_1 ();  // open: B_In, Shift_Rigth, Output, Shift_Left
  _4_bit_and u_4_bit_and_1 ();  // open: A_In, B_In, Output
  _4_bit_or u_4_bit_or_1 ();  // open: A_In, B_In, Output
  _4_bit_xor u_4_bit_xor_1 ();  // open: A_In, B_In, Output
endmodule

// 1-bit Half\nAdder
module _1_bit_half_adder (
  input  A_In,
  input  B_In,
  output Sum_Out,
  output Carry_Out
);

  xor xor_1 (Sum_Out, A_In, B_In);
  and and_1 (Carry_Out, A_In, B_In);
endmodule

// 4-Bit\nFull Adder
module _4_bit_full_adder (
  input  [3:0] A_In,
  input  [3:0] B_In,
  input  Carry_In,
  output Carry_Out,
  output [3:0] Output
);

  wire n1_bit_full_adder_2_carry_out, n1_bit_full_adder_3_carry_out, n1_bit_full_adder_4_carry_out;

  _1_bit_full_adder u_1_bit_full_adder_1 (
    .Carry_In(n1_bit_full_adder_2_carry_out), .A_In(A_In[3]), .B_In(B_In[3]), .Sum_Out(Output[3]),
    .Carry_Out(Carry_Out));
  _1_bit_full_adder u_1_bit_full_adder_2 (
    .Carry_In(n1_bit_full_adder_3_carry_out), .A_In(A_In[2]), .B_In(B_In[2]), .Sum_Out(Output[2]),
    .Carry_Out(n1_bit_full_adder_2_carry_out));
  _1_bit_full_adder u_1_bit_full_adder_3 (
    .Carry_In(n1_bit_full_adder_4_carry_out), .A_In(A_In[1]), .B_In(B_In[1]), .Sum_Out(Output[1]),
    .Carry_Out(n1_bit_full_adder_3_carry_out));
  _1_bit_full_adder u_1_bit_full_adder_4 (
    .Carry_In(Carry_In), .A_In(A_In[0]), .B_In(B_In[0]), .Sum_Out(Output[0]),
    .Carry_Out(n1_bit_full_adder_4_carry_out));
endmodule

// 1-Bit Full\nAdder
module _1_bit_full_adder (
  input  Carry_In,
  input  A_In,
  input  B_In,
  output Sum_Out,
  output Carry_Out
);

  wire n1_bit_half_adder_1_carry_out, n1_bit_half_adder_1_sum_out, n1_bit_half_adder_2_carry_out;

  _1_bit_half_adder u_1_bit_half_adder_1 (
    .A_In(A_In), .B_In(B_In), .Sum_Out(n1_bit_half_adder_1_sum_out), .Carry_Out(n1_bit_half_adder_1_carry_out));
  _1_bit_half_adder u_1_bit_half_adder_2 (
    .A_In(Carry_In), .B_In(n1_bit_half_adder_1_sum_out), .Sum_Out(Sum_Out),
    .Carry_Out(n1_bit_half_adder_2_carry_out));
  or or_1 (Carry_Out, n1_bit_half_adder_2_carry_out, n1_bit_half_adder_1_carry_out);
endmodule

// 4-Bit\nIncrementer
module _4_bit_increment (
  input  [3:0] Input,
  output Carry_Out,
  output [3:0] Output
);

  wire n1_bit_half_adder_2_carry_out, n1_bit_half_adder_3_carry_out, n1_bit_half_adder_4_carry_out;

  _1_bit_half_adder u_1_bit_half_adder_1 (
    .A_In(n1_bit_half_adder_2_carry_out), .B_In(Input[3]), .Sum_Out(Output[3]), .Carry_Out(Carry_Out));
  _1_bit_half_adder u_1_bit_half_adder_2 (
    .A_In(n1_bit_half_adder_3_carry_out), .B_In(Input[2]), .Sum_Out(Output[2]),
    .Carry_Out(n1_bit_half_adder_2_carry_out));
  _1_bit_half_adder u_1_bit_half_adder_3 (
    .A_In(n1_bit_half_adder_4_carry_out), .B_In(Input[1]), .Sum_Out(Output[1]),
    .Carry_Out(n1_bit_half_adder_3_carry_out));
  _1_bit_half_adder u_1_bit_half_adder_4 (
    .A_In(1'b1), .B_In(Input[0]), .Sum_Out(Output[0]), .Carry_Out(n1_bit_half_adder_4_carry_out));
endmodule

// 4-Bit\nDecrementer
module _4_bit_decrementer (
  input  [3:0] A_In,
  output Carry_Out,
  output [3:0] Output
);

  wire n1_bit_full_adder_2_carry_out, n1_bit_full_adder_3_carry_out, n1_bit_full_adder_4_carry_out;

  _1_bit_full_adder u_1_bit_full_adder_1 (
    .Carry_In(n1_bit_full_adder_2_carry_out), .A_In(A_In[3]), .B_In(1'b1), .Sum_Out(Output[3]),
    .Carry_Out(Carry_Out));
  _1_bit_full_adder u_1_bit_full_adder_2 (
    .Carry_In(n1_bit_full_adder_3_carry_out), .A_In(A_In[2]), .B_In(1'b1), .Sum_Out(Output[2]),
    .Carry_Out(n1_bit_full_adder_2_carry_out));
  _1_bit_full_adder u_1_bit_full_adder_3 (
    .Carry_In(n1_bit_full_adder_4_carry_out), .A_In(A_In[1]), .B_In(1'b1), .Sum_Out(Output[1]),
    .Carry_Out(n1_bit_full_adder_3_carry_out));
  _1_bit_full_adder u_1_bit_full_adder_4 (
    .Carry_In(1'b0), .A_In(A_In[0]), .B_In(1'b1), .Sum_Out(Output[0]),
    .Carry_Out(n1_bit_full_adder_4_carry_out));
endmodule

// 4-Bit\nAND
module _4_bit_and (
  input  [3:0] A_In,
  input  [3:0] B_In,
  output [3:0] Output
);

  and and_1 (Output[3], A_In[3], B_In[3]);
  and and_2 (Output[2], A_In[2], B_In[2]);
  and and_3 (Output[1], A_In[1], B_In[1]);
  and and_4 (Output[0], A_In[0], B_In[0]);
endmodule

// 4-Bit\nOR
module _4_bit_or (
  input  [3:0] A_In,
  input  [3:0] B_In,
  output [3:0] Output
);

  or or_1 (Output[3], A_In[3], B_In[3]);
  or or_2 (Output[2], A_In[2], B_In[2]);
  or or_3 (Output[1], A_In[1], B_In[1]);
  or or_4 (Output[0], A_In[0], B_In[0]);
endmodule

// 4-Bit\nXOR
module _4_bit_xor (
  input  [3:0] A_In,
  input  [3:0] B_In,
  output [3:0] Output
);

  xor xor_1 (Output[3], A_In[3], B_In[3]);
  xor xor_2 (Output[2], A_In[2], B_In[2]);
  xor xor_3 (Output[1], A_In[1], B_In[1]);
  xor xor_4 (Output[0], A_In[0], B_In[0]);
endmodule

// 4-Bit\nRight/Left Shift
module _4_bit_right_left_shift (
  input  [3:0] B_In,
  input  Shift_Left,
  input  Shift_Rigth,
  output [3:0] Output
);

  wire and_1_out, and_2_out, and_3_out, and_4_out, and_5_out, and_6_out, and_7_out, and_8_out, and_9_out,
       and_10_out, and_11_out, and_12_out, not_1_out, not_2_out, not_3_out, not_4_out, not_5_out, not_6_out,
       not_7_out, not_8_out;

  and and_1 (and_1_out, Shift_Rigth, 1'b0);
  not not_1 (not_1_out, Shift_Rigth);
  and and_2 (and_2_out, B_In[3], not_1_out, not_2_out);
  or or_1 (Output[3], and_1_out, and_2_out, and_3_out);
  not not_2 (not_2_out, Shift_Left);
  and and_3 (and_3_out, Shift_Left, B_In[2]);
  and and_4 (and_4_out, Shift_Rigth, B_In[3]);
  not not_3 (not_3_out, Shift_Rigth);
  and and_5 (and_5_out, B_In[2], not_3_out, not_4_out);
  or or_2 (Output[2], and_4_out, and_5_out, and_6_out);
  not not_4 (not_4_out, Shift_Left);
  and and_6 (and_6_out, Shift_Left, B_In[1]);
  and and_7 (and_7_out, Shift_Rigth, B_In[2]);
  not not_5 (not_5_out, Shift_Rigth);
  and and_8 (and_8_out, B_In[1], not_5_out, not_6_out);
  or or_3 (Output[1], and_7_out, and_8_out, and_9_out);
  not not_6 (not_6_out, Shift_Left);
  and and_9 (and_9_out, Shift_Left, B_In[0]);
  and and_10 (and_10_out, Shift_Rigth, B_In[1]);
  not not_7 (not_7_out, Shift_Rigth);
  and and_11 (and_11_out, B_In[0], not_7_out, not_8_out);
  or or_4 (Output[0], and_10_out, and_11_out, and_12_out);
  not not_8 (not_8_out, Shift_Left);
  and and_12 (and_12_out, Shift_Left, 1'b0);
endmodule

// 4-Bit One's\nComplement
module _4_bit_ones_complement (
  input  [3:0] Input,
  output [3:0] Output
);

  not not_1 (Output[3], Input[3]);
  not not_2 (Output[2], Input[2]);
  not not_3 (Output[1], Input[1]);
  not not_4 (Output[0], Input[0]);
endmodule

// 4-Bit\nSubtractor
module _4_bit_subtractor (
  input  [3:0] B_In,
  input  [3:0] A_In,
  output Overflow___Underflow,
  output [3:0] Output
);

  wire n4_bit_full_adder_1_carry_out;
  wire [3:0] n4_bit_ones_complement_1_output;

  xor xor_1 (Overflow___Underflow, n4_bit_full_adder_1_carry_out, 1'b1);
  _4_bit_ones_complement u_4_bit_ones_complement_1 (.Input(B_In), .Output(n4_bit_ones_complement_1_output));
  _4_bit_full_adder u_4_bit_full_adder_1 (
    .A_In(A_In), .B_In(n4_bit_ones_complement_1_output), .Output(Output),
    .Carry_Out(n4_bit_full_adder_1_carry_out), .Carry_In(1'b1));
endmodule
